// Logisim project LAB4_done.circ as structural Verilog
// A
module main (
  input  B9,
  input  B9_2,
  input  B8,
  input  B8_2,
  input  B7,
  input  B7_2,
  input  B6,
  input  B6_2,
  input  B5,
  input  B5_2,
  input  B4,
  input  B4_2,
  input  B3,
  input  B3_2,
  input  B2,
  input  B2_2,
  input  B1,
  input  B1_2,
  input  B0,
  input  B0_2
);

  wire _7404_2__2__1y, _7404_2__4__2y, _7404_2__6__3y, _7404_2__8__4y, _7404_2__10__5y, _7404_2__12__6y,
       _7404_3__2__1y, _7404_3__4__2y, _7404_3__6__3y, _7404_5__2__1y, _7404_5__4__2y, _7404_5__6__3y,
       _7404_5__8__4y, _7404_5__10__5y, _7404_5__12__6y, _7404_6__2__1y, _7404_6__4__2y, _7404_6__6__3y,
       _7448_2__9__e, _7448_2__10__d, _7448_2__11__c, _7448_2__12__b, _7448_2__13__a, _7448_2__14__g,
       _7448_2__15__f, _7448_3__9__e, _7448_3__10__d, _7448_3__11__c, _7448_3__12__b, _7448_3__13__a,
       _7448_3__14__g, _7448_3__15__f, _7448_4__9__e, _7448_4__10__d, _7448_4__11__c, _7448_4__12__b,
       _7448_4__13__a, _7448_4__14__g, _7448_4__15__f, _7448__9__e, _7448__10__d, _7448__11__c, _7448__12__b,
       _7448__13__a, _7448__14__g, _7448__15__f, _74185_p7, _74185_p8, _74185_p9, _74185_p10, _74185_p11,
       _74185_p12, _74185_p13, A0, A1, B0_t, B1_t, BIT_0_LED_0, BIT_0_LED_1, BIT_1_LED_0, BIT_1_LED_1,
       BIT_2_LED_0, BIT_2_LED_1, BIT_3_LED_0, BIT_3_LED_1, BTN3, C0, C1, D0, D1, n7483_1_p10, n7483_1_p11,
       n7483_1_p12, n7483_1_p13;

  Chip7404 _7404 (
    ._1__1A(A0), ._2__1Y(BIT_3_LED_0), ._3__2A(B0_t), ._4__2Y(BIT_1_LED_0), ._5__3A(C0),
    ._6__3Y(BIT_0_LED_0), ._13__6A(D0), ._12__6Y(BIT_2_LED_0));  // open: _7__GND, _14__Vcc, _11__5A, _10__5Y, _9__4A, _8__4Y
  Chip7404 _7404_2 (
    ._1__1A(B9), ._2__1Y(_7404_2__2__1y), ._3__2A(B8), ._4__2Y(_7404_2__4__2y), ._5__3A(B7),
    ._6__3Y(_7404_2__6__3y), ._13__6A(B6), ._12__6Y(_7404_2__12__6y), ._11__5A(B5),
    ._10__5Y(_7404_2__10__5y), ._9__4A(B4), ._8__4Y(_7404_2__8__4y));  // open: _7__GND, _14__Vcc
  Chip7404 _7404_3 (
    ._1__1A(B3), ._2__1Y(_7404_3__2__1y), ._3__2A(B2), ._4__2Y(_7404_3__4__2y), ._5__3A(B1),
    ._6__3Y(_7404_3__6__3y));  // open: _7__GND, _14__Vcc, _13__6A, _12__6Y, _11__5A, _10__5Y, _9__4A, _8__4Y
  Chip7448 _7448 (
    ._1__B(BIT_0_LED_0), ._2__C(BIT_1_LED_0), ._3__nLT(1'b1), ._5__nRBI(B0), ._6__D(BIT_3_LED_0),
    ._7__A(BIT_2_LED_0), ._15__f(_7448__15__f), ._14__g(_7448__14__g), ._13__a(_7448__13__a),
    ._12__b(_7448__12__b), ._11__c(_7448__11__c), ._10__d(_7448__10__d), ._9__e(_7448__9__e));  // open: _4__NC, _8__GND, _16__Vcc
  // Sude_Çakmak_Lab4_AdderSubtractor_7483 7483_1: pin names not known; wires that end beside it: BIT_2_LED_0, BIT_2_LED_1, BIT_0_LED_0, BIT_0_LED_1, BIT_1_LED_0, BIT_1_LED_1, BIT_3_LED_0, BIT_3_LED_1, BTN3, n7483_1_p10, n7483_1_p11, n7483_1_p12, n7483_1_p13
  Chip74147 _74147 (
    .B1(_7404_3__6__3y), .B2(_7404_3__4__2y), .B3(_7404_3__2__1y), .B4(_7404_2__8__4y), .B5(_7404_2__10__5y),
    .B6(_7404_2__12__6y), .B7(_7404_2__6__3y), .B8(_7404_2__4__2y), .B9(_7404_2__2__1y), .D(A0), .C(B0_t),
    .B(C0), .A(D0));
  _7_Segment_Display u_7_segment_display_1 (
    .g(_7448__14__g), .f(_7448__15__f), .a(_7448__13__a), .b(_7448__12__b), .e(_7448__9__e),
    .d(_7448__10__d), .c(_7448__11__c));  // open: dp
  // _74185 _74185: pin names not known; wires that end beside it: 1'b0, n7483_1_p13, n7483_1_p12, n7483_1_p11, n7483_1_p10, 1'b0, _74185_p7, _74185_p8, _74185_p9, _74185_p10, _74185_p11, _74185_p12, _74185_p13
  Chip7404 _7404_4 (
    ._1__1A(A1), ._2__1Y(BIT_3_LED_1), ._3__2A(B1_t), ._4__2Y(BIT_1_LED_1), ._5__3A(C1),
    ._6__3Y(BIT_0_LED_1), ._13__6A(D1), ._12__6Y(BIT_2_LED_1));  // open: _7__GND, _14__Vcc, _11__5A, _10__5Y, _9__4A, _8__4Y
  Chip7448 _7448_2 (
    ._1__B(_74185_p9), ._2__C(_74185_p8), ._3__nLT(1'b1), ._5__nRBI(_74185_p7), ._6__D(1'b0),
    ._7__A(_74185_p10), ._15__f(_7448_2__15__f), ._14__g(_7448_2__14__g), ._13__a(_7448_2__13__a),
    ._12__b(_7448_2__12__b), ._11__c(_7448_2__11__c), ._10__d(_7448_2__10__d), ._9__e(_7448_2__9__e));  // open: _4__NC, _8__GND, _16__Vcc
  Chip7404 _7404_5 (
    ._1__1A(B9_2), ._2__1Y(_7404_5__2__1y), ._3__2A(B8_2), ._4__2Y(_7404_5__4__2y), ._5__3A(B7_2),
    ._6__3Y(_7404_5__6__3y), ._13__6A(B6_2), ._12__6Y(_7404_5__12__6y), ._11__5A(B5_2),
    ._10__5Y(_7404_5__10__5y), ._9__4A(B4_2), ._8__4Y(_7404_5__8__4y));  // open: _7__GND, _14__Vcc
  Chip7404 _7404_6 (
    ._1__1A(B3_2), ._2__1Y(_7404_6__2__1y), ._3__2A(B2_2), ._4__2Y(_7404_6__4__2y), ._5__3A(B1_2),
    ._6__3Y(_7404_6__6__3y));  // open: _7__GND, _14__Vcc, _13__6A, _12__6Y, _11__5A, _10__5Y, _9__4A, _8__4Y
  Chip7448 _7448_3 (
    ._1__B(BIT_0_LED_1), ._2__C(BIT_1_LED_1), ._3__nLT(1'b1), ._5__nRBI(B0_2), ._6__D(BIT_3_LED_1),
    ._7__A(BIT_2_LED_1), ._15__f(_7448_3__15__f), ._14__g(_7448_3__14__g), ._13__a(_7448_3__13__a),
    ._12__b(_7448_3__12__b), ._11__c(_7448_3__11__c), ._10__d(_7448_3__10__d), ._9__e(_7448_3__9__e));  // open: _4__NC, _8__GND, _16__Vcc
  _7_Segment_Display u_7_segment_display_2 (
    .g(_7448_4__14__g), .f(_7448_4__15__f), .a(_7448_4__13__a), .b(_7448_4__12__b), .e(_7448_4__9__e),
    .d(_7448_4__10__d), .c(_7448_4__11__c));  // open: dp
  _7_Segment_Display u_7_segment_display_3 (
    .g(_7448_2__14__g), .f(_7448_2__15__f), .a(_7448_2__13__a), .b(_7448_2__12__b), .e(_7448_2__9__e),
    .d(_7448_2__10__d), .c(_7448_2__11__c));  // open: dp
  Chip74147 _74147_2 (
    .B1(_7404_6__6__3y), .B2(_7404_6__4__2y), .B3(_7404_6__2__1y), .B4(_7404_5__8__4y), .B5(_7404_5__10__5y),
    .B6(_7404_5__12__6y), .B7(_7404_5__6__3y), .B8(_7404_5__4__2y), .B9(_7404_5__2__1y), .D(A1), .C(B1_t),
    .B(C1), .A(D1));
  _7_Segment_Display u_7_segment_display_4 (
    .g(_7448_3__14__g), .f(_7448_3__15__f), .a(_7448_3__13__a), .b(_7448_3__12__b), .e(_7448_3__9__e),
    .d(_7448_3__10__d), .c(_7448_3__11__c));  // open: dp
  Chip7448 _7448_4 (
    ._1__B(_74185_p13), ._2__C(_74185_p12), ._3__nLT(1'b1), ._6__D(_74185_p11), ._7__A(BTN3),
    ._15__f(_7448_4__15__f), ._14__g(_7448_4__14__g), ._13__a(_7448_4__13__a), ._12__b(_7448_4__12__b),
    ._11__c(_7448_4__11__c), ._10__d(_7448_4__10__d), ._9__e(_7448_4__9__e));  // open: _4__NC, _5__nRBI, _8__GND, _16__Vcc

  // Other names for the same wires on the sheet: BTN0 = B0; BTN1 = B0_2
endmodule

module Chip7404 (
  input  _1__1A,
  input  _14__Vcc,
  input  _13__6A,
  input  _3__2A,
  input  _11__5A,
  input  _5__3A,
  input  _9__4A,
  input  _7__GND,
  output _2__1Y,
  output _12__6Y,
  output _4__2Y,
  output _10__5Y,
  output _6__3Y,
  output _8__4Y
);

  not not_1 (_2__1Y, _1__1A);
  not not_2 (_4__2Y, _3__2A);
  not not_3 (_6__3Y, _5__3A);
  not not_4 (_12__6Y, _13__6A);
  not not_5 (_10__5Y, _11__5A);
  not not_6 (_8__4Y, _9__4A);

  // Notes on the sheet:
  //   7407: hex inverter
endmodule

module Chip7448 (
  input  _1__B,
  input  _16__Vcc,
  input  _2__C,
  input  _3__nLT,
  input  _4__NC,
  input  _5__nRBI,
  input  _6__D,
  input  _7__A,
  input  _8__GND,
  output _15__f,
  output _14__g,
  output _13__a,
  output _12__b,
  output _11__c,
  output _10__d,
  output _9__e
);

  wire nand_1_out, nand_2_out, nand_3_out, nand_4_out, nand_5_out, nand_6_out, nand_7_out, nand_8_out,
       nand_9_out, nand_10_out, nand_11_out, nand_12_out, nand_13_out, nand_14_out, nand_15_out, nand_16_out,
       nand_17_out, nand_18_out, nand_19_out, nand_20_out, nand_21_out, nand_22_out, nand_23_out,
       nand_24_out, nand_25_out, not_1_out, not_2_out, not_3_out;

  nand nand_1 (nand_1_out, _7__A, _3__nLT);
  nand nand_2 (nand_2_out, _1__B, _3__nLT);
  nand nand_3 (nand_3_out, _2__C, _3__nLT);
  not not_1 (not_1_out, _6__D);
  not not_2 (not_2_out, _5__nRBI);
  nand nand_4 (nand_4_out, nand_1_out, nand_8_out);
  nand nand_5 (nand_5_out, nand_2_out, nand_8_out);
  nand nand_6 (nand_6_out, nand_3_out, nand_8_out);
  nand nand_7 (nand_7_out, not_1_out, nand_8_out);
  nand nand_8 (nand_8_out, _3__nLT, not_2_out, not_1_out, nand_3_out, nand_2_out, nand_1_out);
  nand nand_9 (nand_9_out, nand_5_out, nand_7_out);
  nand nand_10 (nand_10_out, nand_1_out, nand_6_out);
  nand nand_11 (nand_11_out, nand_4_out, nand_2_out, nand_3_out, not_1_out);
  nand nand_12 (nand_12_out, nand_5_out, nand_7_out);
  nand nand_13 (nand_13_out, nand_4_out, nand_2_out, nand_6_out);
  nand nand_14 (nand_14_out, nand_1_out, nand_5_out, nand_6_out);
  nand nand_15 (nand_15_out, nand_6_out, nand_7_out);
  nand nand_16 (nand_16_out, nand_1_out, nand_5_out, nand_3_out);
  nand nand_17 (nand_17_out, nand_4_out, nand_2_out, nand_3_out);
  nand nand_18 (nand_18_out, nand_1_out, nand_2_out, nand_6_out);
  nand nand_19 (nand_19_out, nand_4_out, nand_5_out, nand_6_out);
  not not_3 (not_3_out, nand_4_out);
  nand nand_20 (nand_20_out, nand_2_out, nand_6_out);
  nand nand_21 (nand_21_out, nand_4_out, nand_5_out);
  nand nand_22 (nand_22_out, nand_5_out, nand_3_out);
  nand nand_23 (nand_23_out, nand_4_out, nand_3_out, not_1_out);
  nand nand_24 (nand_24_out, nand_4_out, nand_5_out, nand_6_out);
  nand nand_25 (nand_25_out, nand_2_out, nand_3_out, not_1_out, _3__nLT);
  and and_1 (_13__a, nand_9_out, nand_10_out, nand_11_out);
  and and_2 (_12__b, nand_12_out, nand_13_out, nand_14_out);
  and and_3 (_11__c, nand_15_out, nand_16_out);
  and and_4 (_10__d, nand_17_out, nand_18_out, nand_19_out);
  and and_5 (_9__e, not_3_out, nand_20_out);
  and and_6 (_15__f, nand_21_out, nand_22_out, nand_23_out);
  and and_7 (_14__g, nand_24_out, nand_25_out);

  // Notes on the sheet:
  //   7448: BCD to 7-segment decoder
endmodule

module Chip74147 (
  input  B1,
  input  B2,
  input  B3,
  input  B4,
  input  B5,
  input  B6,
  input  B7,
  input  B8,
  input  B9,
  output D,
  output C,
  output B,
  output A
);

  wire and_1_out, and_2_out, and_3_out, and_4_out, and_5_out, and_6_out, and_7_out, and_8_out, and_9_out,
       and_10_out, and_11_out, and_12_out, and_13_out, and_14_out, and_15_out, and_16_out, and_17_out,
       and_18_out, and_19_out, and_20_out, and_21_out, and_22_out, and_23_out, and_24_out, and_25_out,
       and_26_out, and_27_out, and_28_out, and_29_out, and_30_out, and_31_out, and_32_out, and_33_out,
       and_34_out, and_35_out, and_36_out, and_37_out, and_38_out, and_39_out, and_40_out, and_41_out,
       and_42_out, and_43_out, and_44_out, and_45_out, not_1_out, not_2_out, not_3_out, not_4_out, not_5_out,
       not_6_out, not_7_out, not_8_out, not_9_out, not_10_out, not_11_out, not_12_out, not_13_out,
       not_14_out, not_15_out, not_16_out, not_17_out, not_18_out, not_19_out, not_20_out, not_21_out,
       not_22_out, not_23_out, not_24_out, not_25_out, not_26_out, not_27_out, not_28_out, not_29_out,
       not_30_out, not_31_out, not_32_out, not_33_out, not_34_out, not_35_out, not_36_out, not_37_out,
       not_38_out, not_39_out, not_40_out, not_41_out, not_42_out, not_43_out, not_44_out, not_45_out,
       not_46_out, not_47_out, not_48_out, not_49_out, not_50_out, not_51_out, not_52_out, not_53_out,
       not_54_out, not_55_out, not_56_out, not_57_out, not_58_out, not_59_out, not_60_out, not_61_out,
       not_62_out, not_63_out, not_64_out, not_65_out, not_66_out, not_67_out, not_68_out, not_69_out,
       not_70_out, not_71_out, not_72_out, not_73_out;

  not not_1 (not_1_out, B2);
  not not_2 (not_2_out, B3);
  not not_3 (not_3_out, B4);
  not not_4 (not_4_out, B6);
  not not_5 (not_5_out, B1);
  not not_6 (not_6_out, B5);
  not not_7 (not_7_out, B6);
  not not_8 (not_8_out, B8);
  not not_9 (not_9_out, B3);
  not not_10 (not_10_out, B8);
  not not_11 (not_11_out, B4);
  not not_12 (not_12_out, B6);
  not not_13 (not_13_out, B7);
  not not_14 (not_14_out, B8);
  not not_15 (not_15_out, B2);
  not not_16 (not_16_out, B8);
  not not_17 (not_17_out, B1);
  not not_18 (not_18_out, B8);
  not not_19 (not_19_out, B5);
  not not_20 (not_20_out, B8);
  not not_21 (not_21_out, B8);
  not not_22 (not_22_out, B8);
  not not_23 (not_23_out, B8);
  not not_24 (not_24_out, B4);
  not not_25 (not_25_out, B8);
  not not_26 (not_26_out, B8);
  not not_27 (not_27_out, B1);
  not not_28 (not_28_out, B5);
  not not_29 (not_29_out, B6);
  not not_30 (not_30_out, B8);
  not not_31 (not_31_out, B3);
  not not_32 (not_32_out, B8);
  not not_33 (not_33_out, B4);
  not not_34 (not_34_out, B6);
  not not_35 (not_35_out, B7);
  not not_36 (not_36_out, B8);
  not not_37 (not_37_out, B2);
  not not_38 (not_38_out, B8);
  not not_39 (not_39_out, B4);
  not not_40 (not_40_out, B5);
  not not_41 (not_41_out, B1);
  not not_42 (not_42_out, B8);
  not not_43 (not_43_out, B5);
  not not_44 (not_44_out, B8);
  not not_45 (not_45_out, B6);
  not not_46 (not_46_out, B8);
  not not_47 (not_47_out, B8);
  not not_48 (not_48_out, B8);
  not not_49 (not_49_out, B8);
  not not_50 (not_50_out, B1);
  not not_51 (not_51_out, B5);
  not not_52 (not_52_out, B6);
  not not_53 (not_53_out, B8);
  not not_54 (not_54_out, B3);
  not not_55 (not_55_out, B8);
  not not_56 (not_56_out, B4);
  not not_57 (not_57_out, B6);
  not not_58 (not_58_out, B7);
  not not_59 (not_59_out, B8);
  not not_60 (not_60_out, B6);
  not not_61 (not_61_out, B2);
  not not_62 (not_62_out, B8);
  not not_63 (not_63_out, B4);
  not not_64 (not_64_out, B1);
  not not_65 (not_65_out, B8);
  not not_66 (not_66_out, B5);
  not not_67 (not_67_out, B8);
  not not_68 (not_68_out, B2);
  not not_69 (not_69_out, B8);
  not not_70 (not_70_out, B8);
  not not_71 (not_71_out, B8);
  and and_1 (and_1_out, not_1_out, B8, B9);
  and and_2 (and_2_out, not_2_out, B8, B9);
  and and_3 (and_3_out, not_3_out, B8, B9);
  and and_4 (and_4_out, not_4_out, B8, B9);
  and and_5 (and_5_out, B7, B8, B9);
  and and_6 (and_6_out, B5, B8, B9);
  and and_7 (and_7_out, B1, B8, B9);
  and and_8 (and_8_out, not_5_out, not_6_out, not_7_out, not_8_out);
  and and_9 (and_9_out, not_9_out, not_10_out);
  and and_10 (and_10_out, not_11_out, not_12_out, not_13_out, not_14_out);
  not not_72 (not_72_out, B9);
  and and_11 (and_11_out, not_15_out, B6, not_16_out);
  and and_12 (and_12_out, not_17_out, B4, not_18_out);
  and and_13 (and_13_out, B4, not_19_out, not_20_out);
  and and_14 (and_14_out, B4, B7, not_21_out);
  and and_15 (and_15_out, B4, B5, B6, B7);
  and and_16 (and_16_out, B2, B7, not_22_out);
  and and_17 (and_17_out, B2, B5, not_23_out);
  and and_18 (and_18_out, B1, not_24_out, B5, not_25_out);
  and and_19 (and_19_out, B1, B2, not_26_out);
  and and_20 (and_20_out, not_27_out, not_28_out, not_29_out, not_30_out);
  and and_21 (and_21_out, not_31_out, not_32_out);
  and and_22 (and_22_out, not_33_out, not_34_out, not_35_out, not_36_out);
  not not_73 (not_73_out, B9);
  and and_23 (and_23_out, not_37_out, B6, not_38_out);
  and and_24 (and_24_out, not_39_out, B6, B7);
  and and_25 (and_25_out, not_40_out, B6, B7);
  and and_26 (and_26_out, not_41_out, B4, not_42_out);
  and and_27 (and_27_out, B4, not_43_out, not_44_out);
  and and_28 (and_28_out, B2, not_45_out, not_46_out);
  and and_29 (and_29_out, B2, B5, not_47_out);
  and and_30 (and_30_out, B2, B3, B6, B7);
  and and_31 (and_31_out, B1, B5, B7, not_48_out);
  and and_32 (and_32_out, B1, B2, not_49_out);
  and and_33 (and_33_out, not_50_out, not_51_out, not_52_out, not_53_out, B9);
  and and_34 (and_34_out, not_54_out, not_55_out, B9);
  and and_35 (and_35_out, not_56_out, not_57_out, not_58_out, not_59_out, B9);
  and and_36 (and_36_out, not_60_out, B7, B8, B9);
  and and_37 (and_37_out, not_61_out, B6, not_62_out, B9);
  and and_38 (and_38_out, not_63_out, B5, B6, B7, B9);
  and and_39 (and_39_out, not_64_out, B4, not_65_out, B9);
  and and_40 (and_40_out, B4, not_66_out, not_67_out, B9);
  and and_41 (and_41_out, not_68_out, B3, B4, B5, B7, B9);
  and and_42 (and_42_out, B2, B7, not_69_out, B9);
  and and_43 (and_43_out, B2, B5, not_70_out, B9);
  and and_44 (and_44_out, B1, B6, not_71_out, B9);
  and and_45 (and_45_out, B1, B3, B5, B7, B9);
  or or_1 (D, and_1_out, and_2_out, and_3_out, and_4_out, and_5_out, and_6_out, and_7_out);
  or or_2 (C, and_8_out, and_9_out, and_10_out, not_72_out, and_11_out, and_12_out, and_13_out, and_14_out, and_15_out, and_16_out, and_17_out, and_18_out, and_19_out);
  or or_3 (B, and_20_out, and_21_out, and_22_out, not_73_out, and_23_out, and_24_out, and_25_out, and_26_out, and_27_out, and_28_out, and_29_out, and_30_out, and_31_out, and_32_out);
  or or_4 (A, and_33_out, and_34_out, and_35_out, and_36_out, and_37_out, and_38_out, and_39_out, and_40_out, and_41_out, and_42_out, and_43_out, and_44_out, and_45_out);
endmodule

module _7483 (
  input  B2,
  input  A2,
  input  B2_2,
  input  A2_2,
  input  B1,
  input  A1,
  input  C1,
  output S1,
  output S1_2
);

  wire and_1_out, and_2_out, and_3_out, and_4_out, and_5_out, and_6_out, buffer_1_out, buffer_2_out,
       nand_1_out, nand_2_out, nand_3_out, nor_1_out, nor_2_out, nor_3_out, nor_4_out, not_1_out, not_2_out,
       not_3_out, not_4_out, not_5_out, xnor_1_out;

  not not_1 (not_1_out, C1);
  nand nand_1 (nand_1_out, B2, A2);
  nor nor_1 (nor_1_out, B2, A2);
  nand nand_2 (nand_2_out, B2_2, A2_2);
  nor nor_2 (nor_2_out, B2_2, A2_2);
  nand nand_3 (nand_3_out, B1, A1);
  nor nor_3 (nor_3_out, B1, A1);
  not not_2 (not_2_out, nor_1_out);
  buf buffer_1 (buffer_1_out, nor_2_out);
  // AND_Gate and_1 has open pins: out=and_1_out
  // AND_Gate and_2 has open pins: out=and_2_out
  not not_3 (not_3_out, nor_2_out);
  buf buffer_2 (buffer_2_out, nor_3_out);
  and and_3 (and_3_out, nand_3_out, not_1_out);
  not not_4 (not_4_out, nor_3_out);
  not not_5 (not_5_out, not_1_out);
  and and_4 (and_4_out, nand_1_out, not_2_out);
  NotExactlyOne xnor_1 (.out(xnor_1_out), .in0(buffer_1_out), .in1(and_1_out), .in2(and_2_out));
  and and_5 (and_5_out, nand_2_out, not_3_out);
  nor nor_4 (nor_4_out, buffer_2_out, and_3_out);
  and and_6 (and_6_out, nand_3_out, not_4_out);
  xor xor_1 (S1, and_5_out, nor_4_out);
  // XOR_Gate xor_2 has open pins: in0=and_4_out, in1=xnor_1_out, out=open
  xor xor_3 (S1_2, and_6_out, not_5_out);
endmodule

module test (
  input  _1,
  input  _2,
  input  a3,
  input  b4,
  input  _5,
  input  _6,
  output s1,
  output s2,
  output s3
);

  nand nand_1 (s1, _1, _2);
  ExactlyOne xor_1 (.out(s2), .in1(a3), .in3(b4), .in4(b4));
  // XNOR_Gate xnor_1 is placed but not wired
  or or_1 (s3, _5, _6);
  // NOT_Gate not_1 is placed but not wired
endmodule
